# Fritzing sketch ESP32CamBridgeNodeMCU (saved by Fritzing 0.9.9b)

parts:
  ESP32_-_Back1 = ESP32 - CAM
  U1 = ESP8266 NodeMCU LoLin module

nets:
  N1: ESP32_-_Back1.5V, U1.VU
  N2: ESP32_-_Back1.GPIO0, ESP32_-_Back1.GND#12
  N3: ESP32_-_Back1.GPIO3_/_RX, U1.RX
  N4: ESP32_-_Back1.GPIO1_/_TX, U1.TX
  N5: ESP32_-_Back1.GND#16, U1.GND, U1.EN

custom parts:
  ESP32 - CAM: The ESP32-CAM has a very competitive small-size camera module that can operate independently as a minimum system with a footprint of only 27*40.5*4.5mm and a deep sleep current of up to 6mA.
  ESP8266 NodeMCU LoLin module: ESP8266 based NodeMCU
